// Logisim project Final Sequential Minimal-SOP.circ as structural Verilog: 1 circuit, main circuit main
module main (
  input  in_1,
  input  in_2
);

  wire A_q, A_qn, and_1_out, and_2_out, and_3_out, and_4_out, and_5_out, and_6_out, and_7_out, and_8_out,
       and_9_out, and_10_out, and_11_out, and_12_out, and_13_out, and_14_out, and_15_out, and_16_out,
       and_17_out, and_18_out, and_19_out, B_q, C_q, C_qn, clock_1_out, D_q, not_1_out, not_2_out, not_3_out,
       not_4_out, not_5_out, not_6_out, not_7_out, not_8_out, not_9_out, not_10_out, not_11_out, not_12_out,
       not_13_out, not_14_out, not_15_out, not_16_out, not_17_out, not_18_out, not_19_out, not_20_out,
       or_1_out, or_2_out, or_3_out, or_4_out, or_5_out, or_6_out, or_7_out, or_8_out, or_9_out, or_10_out,
       or_11_out;

  Clock clock_1 (.out(clock_1_out));
  or or_1 (or_1_out, or_2_out, and_3_out);
  or or_2 (or_2_out, and_1_out, and_2_out);
  or or_3 (or_3_out, and_4_out, and_5_out);
  T_Flip_Flop A (.clk(clock_1_out), .T(or_2_out), .Q(A_q), .Qn(A_qn), .preset(in_1), .reset(in_2));  // open: en
  T_Flip_Flop B (.clk(clock_1_out), .T(or_1_out), .Q(B_q), .preset(in_1), .reset(in_2));  // open: Qn, en
  T_Flip_Flop C (.clk(clock_1_out), .T(or_3_out), .Q(C_q), .Qn(C_qn), .preset(in_1), .reset(in_2));  // open: en
  T_Flip_Flop D (.clk(clock_1_out), .T(1'b1), .Q(D_q), .preset(in_1), .reset(in_2));  // open: Qn, en
  and and_1 (and_1_out, C_qn, A_q);
  and and_2 (and_2_out, A_qn, B_q, C_q);
  and and_3 (and_3_out, C_q, D_q);
  and and_4 (and_4_out, A_qn, D_q);
  and and_5 (and_5_out, A_q, B_q, C_q);
  not not_1 (not_1_out, B_q);
  not not_2 (not_2_out, C_q);
  and and_6 (and_6_out, not_2_out, not_3_out);
  not not_3 (not_3_out, D_q);
  not not_4 (not_4_out, B_q);
  and and_7 (and_7_out, not_4_out, C_q);
  not not_5 (not_5_out, C_q);
  not not_6 (not_6_out, C_q);
  and and_8 (and_8_out, not_6_out, D_q);
  and and_9 (and_9_out, B_q, not_7_out);
  not not_7 (not_7_out, C_q);
  not not_8 (not_8_out, B_q);
  not not_9 (not_9_out, C_q);
  and and_10 (and_10_out, not_9_out, not_10_out);
  not not_10 (not_10_out, D_q);
  not not_11 (not_11_out, B_q);
  and and_11 (and_11_out, not_11_out, not_12_out);
  not not_12 (not_12_out, D_q);
  not not_13 (not_13_out, B_q);
  and and_12 (and_12_out, not_13_out, C_q);
  not not_14 (not_14_out, B_q);
  and and_13 (and_13_out, not_14_out, not_15_out);
  not not_15 (not_15_out, C_q);
  not not_16 (not_16_out, B_q);
  and and_14 (and_14_out, not_16_out, not_17_out);
  not not_17 (not_17_out, D_q);
  not not_18 (not_18_out, B_q);
  and and_15 (and_15_out, not_18_out, D_q);
  not not_19 (not_19_out, B_q);
  and and_16 (and_16_out, not_19_out, C_q);
  not not_20 (not_20_out, D_q);
  or or_4 (or_4_out, not_1_out, and_6_out);
  and and_17 (and_17_out, and_7_out, D_q);
  and and_18 (and_18_out, B_q, not_5_out);
  or or_5 (or_5_out, and_8_out, and_9_out);
  or or_6 (or_6_out, not_8_out, and_10_out);
  or or_7 (or_7_out, and_11_out, and_12_out);
  or or_8 (or_8_out, and_13_out, and_14_out);
  or or_9 (or_9_out, and_15_out, and_16_out);
  and and_19 (and_19_out, B_q, not_20_out);
  or or_10 (or_10_out, and_17_out, and_18_out);
  or or_11 (or_11_out, or_9_out, and_19_out);
  _7_Segment_Display u_7_segment_display_1 (
    .g(or_11_out), .f(or_8_out), .a(or_4_out), .b(or_10_out), .e(or_7_out), .d(or_6_out), .c(or_5_out));  // open: dp
endmodule
